# Fritzing sketch WxM_INT (saved by Fritzing 0.9.2b)
circuit board: 8.46667cm x 5.64444cm
breadboards: 1

parts:
  Part1 = Arduino Pro Mini v13
  NRF24L1 = NRF24L01
  Part2 = FTDI Basic Programmer
  U1 = DIODE-ZENER [package=diode-zener]  # not connected
  R1 = Resistor [tolerance=±2% resistance=1M package=THT]
  C2 = Capacitor Polarized [package=cpol-radial-10uf-25v]
  BAT1 = BATTERY-2 [package=battery-aa]  # not connected
  BAT2 = BATTERY-2 [package=battery-aa]  # not connected
  BAT3 = BATTERY-2 [package=battery-aa]  # not connected
  Solar_Cell1 = 5V 100mA Polycrystalline PET Solar Cell [part_number=IM130407002]  # not connected
  R2 = Resistor [tolerance=±2% resistance=1M package=THT]
  GY1 = MPU-6050 Board GY-521 [form="♀ (female)" package=THT]  # not connected
  Part3 = Barometric Pressure Sensor - BMP085 Breakout  # not connected
  Part5 = Digital Temperature Sensor Breakout - TMP102  # not connected
  U2 = DIODE-ZENER [package=diode-zener]  # not connected
  R3 = Resistor [tolerance=±2% resistance=1M package=THT]
  R4 = Resistor [tolerance=±2% resistance=1M package=THT]
  U3 = DIODE-ZENER [package=diode-zener]  # not connected
  R5 = Resistor [tolerance=±2% resistance=1M package=THT]
  R6 = Resistor [tolerance=±2% resistance=1M package=THT]

nets:
  N1: Part1.DTR, Part2.DTR
  N2: Part1.D0/TX, Part2.RXI
  N3: Part1.D1/RX, Part2.TXO
  VCC: Part1.VCC, NRF24L1.VCC, Part2.POWER, C2.+
  GND: Part1.GND, NRF24L1.GND, Part2.CTS, Part2.GND, C2.-
  N4: R1.Pin_1, R2.Pin_0
  N5: R3.Pin_1, R4.Pin_0
  N6: R5.Pin_1, R6.Pin_0

notes:
  under construction...

custom parts:
  NRF24L01: NRF24L01 module
  5V 100mA Polycrystalline PET Solar Cell: This is 5V 100mA Polycrystalline PET Solar Cell. It is high quality and exquisite appearance. It is used in all kinds of high-grade electronic products.
  MPU-6050 Board GY-521: Acelerometro y Giroscopio MPU-6050 Board GY-521
